# Fritzing sketch enchantedorbs (saved by Fritzing 0.9.2b)
breadboards: 1

parts:
  Part1 = Arduino Mega 2560 (Rev3)
  Part2 = Arduino Motor Shield

nets:
  GND: Part1.GND, Part2.GND
  N1: Part1.D9_PWM, Part2.D9
  3V3: Part1.3V3, Part2.3.3V
  5V: Part1.5V, Part2.5V
  N2: Part1.D50, Part2.D12
  N3: Part1.D51, Part2.D11
  N4: Part1.D52, Part2.D13
